# Fritzing sketch Untitled Sketch 2 (saved by Fritzing 0.9.3b)
breadboards: 1

parts:
  Raspberry_Pi_1 = Raspberry Pi 3 [part_number=RPI-3-V1.2]
  U1 = TRANSCHIPTC5747 [package=camera_sfv24r-2st_2]  # not connected
  J1 = Basic Servo
  J2 = Basic Servo
  VCC1 = Battery  # not connected

nets:
  N1: Raspberry_Pi_1.GND, J1.pulse
  N2: Raspberry_Pi_1.GIPO14, J2.pulse
